// Logisim project sleepyu.circ as structural Verilog: 6 circuits, main circuit main
module main (
);

  wire PC_Clock_out;
  wire [7:0] adder_1_out, PC_q, undriven;

  Adder adder_1 (.a(8'h1), .b(undriven), .out(adder_1_out));  // open: cin, cout
  Clock PC_Clock (.out(PC_Clock_out));
  Register PC (.D(adder_1_out), .en(1'b1), .clk(PC_Clock_out), .Q(PC_q));  // open: clr
  Instruction_Fetching instruction_fetching_1 ();
  Instruction_Decoding instruction_decoding_1 ();
  Execution execution_1 ();
  Memory_Access memory_access_1 ();
  Write_Back write_back_1 ();

  // Notes on the sheet:
  //   Names: Yash Parmar & Nikunj Patel
  //   Pledge: I pledge my honor that I have abided by the Stevens Honor System.
  //   Implement Execution Stage
  //   Implement Memory Access Stage
  //   Implement Write Back Stage
  //   Implement Instruction Fetching Stage
  //   Implement Instruction Decoding Stage
endmodule

module Instruction_Fetching (
);


  // Notes on the sheet:
  //   Instruction Fetching Stage
endmodule

module Instruction_Decoding (
);


  // Notes on the sheet:
  //   Instruction Decoding Stage
endmodule

module Execution (
);


  // Notes on the sheet:
  //   Execution Stage
endmodule

module Memory_Access (
);


  // Notes on the sheet:
  //   Memory Access Stage
endmodule

module Write_Back (
);


  // Notes on the sheet:
  //   Write Back Stage
endmodule
